// Logisim project calculatorCPU.circ as structural Verilog: 16 circuits, main circuit main
module main (
);

  wire _0_out, _1_out, _2_out, _3_out, _4_out, _5_out, _6_out, _7_out, _8_out, _9_out, alu_1_zero, and_1_out,
       and_2_out, button_2_out, button_3_out, button_4_out, button_5_out, button_out, C_out, clock_1_out,
       control_unit_1_aluop0, control_unit_1_aluop1, control_unit_1_alusrc, control_unit_1_bne,
       control_unit_1_branch, control_unit_1_jump, control_unit_1_regdst, control_unit_1_regwrite,
       control_unit_1_zeroextendimm, keypad_controller_1_write, multiplexer_6_out, not_1_out;
  wire [1:0] shift_operations_1_aluop2;
  wire [2:0] lcd_controller_1__7_segment_0_2, lcd_controller_1__7_segment_2_2,
       lcd_controller_1__7_segment_3_2, lcd_controller_1__7_segment_4_2, lcd_controller_1__7_segment_6_2,
       lcd_controller_1__7_segment_7_2, lcd_controller_1__7_segment_8_2, lcd_controller_1_minus_2;
  wire [3:0] alu_control_1_operation, lcd_controller_1__7_segment_0, lcd_controller_1__7_segment_2,
       lcd_controller_1__7_segment_3, lcd_controller_1__7_segment_4, lcd_controller_1__7_segment_6,
       lcd_controller_1__7_segment_7, lcd_controller_1__7_segment_8, lcd_controller_1_minus;
  wire [4:0] multiplexer_1_out;
  wire [5:0] multiplexer_3_out;
  wire [6:0] lcd_controller_1__7_segment_1, lcd_controller_1__7_segment_5, lcd_controller_1__7_segment_9;
  wire [15:0] adder_1_out, adder_2_out, multiplexer_4_out, multiplexer_5_out, PC_q;
  wire [25:0] SLL_2_output;
  wire [27:0] bit_extender_1_out;
  wire [31:0] alu_1_result, instruction_memory_1_machinecode, keypad_controller_1_output, multiplexer_2_out,
       register_file_1_read_data_1, register_file_1_read_data_2, register_file_1_t8_to_lcd,
       register_file_1_t9_to_keypad, sign_extend_1_out_3, SLL_2_2_output;

  Clock clock_1 (.out(clock_1_out));
  _7_Segment_Display u_7_segment_display_1 (
    .g(lcd_controller_1_minus[0]), .f(lcd_controller_1_minus[1]), .a(lcd_controller_1_minus[2]),
    .b(lcd_controller_1_minus[3]), .e(lcd_controller_1_minus_2[0]), .d(lcd_controller_1_minus_2[1]),
    .c(lcd_controller_1_minus_2[2]));  // open: dp
  _7_Segment_Display u_7_segment_display_2 (
    .g(lcd_controller_1__7_segment_9[0]), .f(lcd_controller_1__7_segment_9[1]),
    .a(lcd_controller_1__7_segment_9[2]), .b(lcd_controller_1__7_segment_9[3]),
    .e(lcd_controller_1__7_segment_9[4]), .d(lcd_controller_1__7_segment_9[5]),
    .c(lcd_controller_1__7_segment_9[6]));  // open: dp
  LCD_Controller lcd_controller_1 (
    .From__t8(register_file_1_t8_to_lcd), .Minus({lcd_controller_1_minus_2, lcd_controller_1_minus}),
    ._7_Segment_9(lcd_controller_1__7_segment_9),
    ._7_Segment_8({lcd_controller_1__7_segment_8_2, lcd_controller_1__7_segment_8}),
    ._7_Segment_7({lcd_controller_1__7_segment_7_2, lcd_controller_1__7_segment_7}),
    ._7_Segment_6({lcd_controller_1__7_segment_6_2, lcd_controller_1__7_segment_6}),
    ._7_Segment_5(lcd_controller_1__7_segment_5),
    ._7_Segment_4({lcd_controller_1__7_segment_4_2, lcd_controller_1__7_segment_4}),
    ._7_Segment_3({lcd_controller_1__7_segment_3_2, lcd_controller_1__7_segment_3}),
    ._7_Segment_2({lcd_controller_1__7_segment_2_2, lcd_controller_1__7_segment_2}),
    ._7_Segment_1(lcd_controller_1__7_segment_1),
    ._7_Segment_0({lcd_controller_1__7_segment_0_2, lcd_controller_1__7_segment_0}));
  Keypad_Controller keypad_controller_1 (
    .C(C_out), .in_2(button_out), .in_3(button_5_out), .in_4(button_4_out), .in_5(button_3_out),
    .in_6(button_2_out), ._9(_9_out), ._8(_8_out), ._7(_7_out), ._6(_6_out), ._5(_5_out), ._4(_4_out),
    ._3(_3_out), ._2(_2_out), ._1(_1_out), ._0(_0_out), .From__t9(register_file_1_t9_to_keypad),
    .Write(keypad_controller_1_write), .Output(keypad_controller_1_output));
  _7_Segment_Display u_7_segment_display_3 (
    .g(lcd_controller_1__7_segment_8[0]), .f(lcd_controller_1__7_segment_8[1]),
    .a(lcd_controller_1__7_segment_8[2]), .b(lcd_controller_1__7_segment_8[3]),
    .e(lcd_controller_1__7_segment_8_2[0]), .d(lcd_controller_1__7_segment_8_2[1]),
    .c(lcd_controller_1__7_segment_8_2[2]));  // open: dp
  _7_Segment_Display u_7_segment_display_4 (
    .g(lcd_controller_1__7_segment_7[0]), .f(lcd_controller_1__7_segment_7[1]),
    .a(lcd_controller_1__7_segment_7[2]), .b(lcd_controller_1__7_segment_7[3]),
    .e(lcd_controller_1__7_segment_7_2[0]), .d(lcd_controller_1__7_segment_7_2[1]),
    .c(lcd_controller_1__7_segment_7_2[2]));  // open: dp
  _7_Segment_Display u_7_segment_display_5 (
    .g(lcd_controller_1__7_segment_6[0]), .f(lcd_controller_1__7_segment_6[1]),
    .a(lcd_controller_1__7_segment_6[2]), .b(lcd_controller_1__7_segment_6[3]),
    .e(lcd_controller_1__7_segment_6_2[0]), .d(lcd_controller_1__7_segment_6_2[1]),
    .c(lcd_controller_1__7_segment_6_2[2]));  // open: dp
  _7_Segment_Display u_7_segment_display_6 (
    .g(lcd_controller_1__7_segment_5[0]), .f(lcd_controller_1__7_segment_5[1]),
    .a(lcd_controller_1__7_segment_5[2]), .b(lcd_controller_1__7_segment_5[3]),
    .e(lcd_controller_1__7_segment_5[4]), .d(lcd_controller_1__7_segment_5[5]),
    .c(lcd_controller_1__7_segment_5[6]));  // open: dp
  Button _7 (.out(_7_out));
  Button _4 (.out(_4_out));
  Button _1 (.out(_1_out));
  Button _0 (.out(_0_out));
  _7_Segment_Display u_7_segment_display_7 (
    .g(lcd_controller_1__7_segment_3[0]), .f(lcd_controller_1__7_segment_3[1]),
    .a(lcd_controller_1__7_segment_3[2]), .b(lcd_controller_1__7_segment_3[3]),
    .e(lcd_controller_1__7_segment_3_2[0]), .d(lcd_controller_1__7_segment_3_2[1]),
    .c(lcd_controller_1__7_segment_3_2[2]));  // open: dp
  _7_Segment_Display u_7_segment_display_8 (
    .g(lcd_controller_1__7_segment_4[0]), .f(lcd_controller_1__7_segment_4[1]),
    .a(lcd_controller_1__7_segment_4[2]), .b(lcd_controller_1__7_segment_4[3]),
    .e(lcd_controller_1__7_segment_4_2[0]), .d(lcd_controller_1__7_segment_4_2[1]),
    .c(lcd_controller_1__7_segment_4_2[2]));  // open: dp
  Button _8 (.out(_8_out));
  Button _5 (.out(_5_out));
  Button _2 (.out(_2_out));
  Button C (.out(C_out));
  _7_Segment_Display u_7_segment_display_9 (
    .g(lcd_controller_1__7_segment_2[0]), .f(lcd_controller_1__7_segment_2[1]),
    .a(lcd_controller_1__7_segment_2[2]), .b(lcd_controller_1__7_segment_2[3]),
    .e(lcd_controller_1__7_segment_2_2[0]), .d(lcd_controller_1__7_segment_2_2[1]),
    .c(lcd_controller_1__7_segment_2_2[2]));  // open: dp
  _7_Segment_Display u_7_segment_display_10 (
    .g(lcd_controller_1__7_segment_1[0]), .f(lcd_controller_1__7_segment_1[1]),
    .a(lcd_controller_1__7_segment_1[2]), .b(lcd_controller_1__7_segment_1[3]),
    .e(lcd_controller_1__7_segment_1[4]), .d(lcd_controller_1__7_segment_1[5]),
    .c(lcd_controller_1__7_segment_1[6]));  // open: dp
  Button _9 (.out(_9_out));
  Button _6 (.out(_6_out));
  Button _3 (.out(_3_out));
  Button button (.out(button_out));
  _7_Segment_Display u_7_segment_display_11 (
    .g(lcd_controller_1__7_segment_0[0]), .f(lcd_controller_1__7_segment_0[1]),
    .a(lcd_controller_1__7_segment_0[2]), .b(lcd_controller_1__7_segment_0[3]),
    .e(lcd_controller_1__7_segment_0_2[0]), .d(lcd_controller_1__7_segment_0_2[1]),
    .c(lcd_controller_1__7_segment_0_2[2]));  // open: dp
  Button button_2 (.out(button_2_out));
  Button button_3 (.out(button_3_out));
  Button button_4 (.out(button_4_out));
  Button button_5 (.out(button_5_out));
  Register #(.width(16)) PC (.D(multiplexer_5_out), .Q(PC_q), .clk(clock_1_out));  // open: en, clr
  Instruction_Memory instruction_memory_1 (._16BitInput(PC_q), .MachineCode(instruction_memory_1_machinecode));
  Shift_Left_26_bIt SLL_2 (.Input(instruction_memory_1_machinecode[25:0]), .ShiftAmt(5'b00010), .Output(SLL_2_output));
  Control_Unit control_unit_1 (
    .OpCode(instruction_memory_1_machinecode[31:26]), .RegDst(control_unit_1_regdst),
    .Jump(control_unit_1_jump), .Branch(control_unit_1_branch), .ALUOp0(control_unit_1_aluop0),
    .ALUSrc(control_unit_1_alusrc), .RegWrite(control_unit_1_regwrite), .ALUOp1(control_unit_1_aluop1),
    .ZeroExtendImm(control_unit_1_zeroextendimm), .BNE(control_unit_1_bne));  // open: MemRead, MemtoReg, MemWrite
  assign bit_extender_1_out = {{2{1'b0}}, SLL_2_output};  // Bit_Extender bit_extender_1
  Adder #(.width(16)) adder_1 (.a(PC_q), .b(16'h1), .out(adder_1_out));  // open: cin, cout
  Register_File register_file_1 (
    .Read_Register_1(instruction_memory_1_machinecode[25:21]),
    .Read_Register_2(instruction_memory_1_machinecode[20:16]), .Write_Register(multiplexer_1_out),
    .Write_Data(alu_1_result), .Write_to__t9_From_Keypad(keypad_controller_1_output),
    .Write_signal_from_keypad(keypad_controller_1_write), .Write(control_unit_1_regwrite),
    .Clock(clock_1_out), .Read_Data_1(register_file_1_read_data_1),
    .Read_Data_2(register_file_1_read_data_2), .t8_To_LCD(register_file_1_t8_to_lcd),
    .T9_to_Keypad(register_file_1_t9_to_keypad));
  Multiplexer #(.width(5), .enable("false")) multiplexer_1 (
    .in0(instruction_memory_1_machinecode[20:16]), .in1(instruction_memory_1_machinecode[15:11]),
    .out(multiplexer_1_out), .sel(control_unit_1_regdst));
  Sign_Extend sign_extend_1 (
    .Input(instruction_memory_1_machinecode[15:0]), .Zero(control_unit_1_zeroextendimm),
    .out_3(sign_extend_1_out_3));
  Shift_Left SLL_2_2 (.Input(sign_extend_1_out_3), .ShiftAmt(5'b00010), .Output(SLL_2_2_output));
  Multiplexer #(.width(32), .enable("false")) multiplexer_2 (
    .in0(register_file_1_read_data_2), .in1(sign_extend_1_out_3), .out(multiplexer_2_out),
    .sel(control_unit_1_alusrc));
  Shift_Operations shift_operations_1 (
    .Funct(instruction_memory_1_machinecode[5:0]), .ALUOp2(shift_operations_1_aluop2[0]),
    .ALUOp3(shift_operations_1_aluop2[1]));
  not not_1 (not_1_out, alu_1_zero);
  ALU alu_1 (
    .A(register_file_1_read_data_1), .B(multiplexer_2_out), .Shamt(instruction_memory_1_machinecode[10:6]),
    .Binvert(1'b0), .CarryIn(1'b0), .Operation(alu_control_1_operation),
    .ShiftOperation(shift_operations_1_aluop2), .Zero(alu_1_zero), .Result(alu_1_result));  // open: CarryOut, Set
  Multiplexer #(.width(6), .enable("false")) multiplexer_3 (
    .in0(instruction_memory_1_machinecode[5:0]), .in1({6{1'b0}}), .out(multiplexer_3_out),
    .sel(control_unit_1_alusrc));
  Adder #(.width(16)) adder_2 (.a(adder_1_out), .b(SLL_2_2_output[17:2]), .out(adder_2_out));  // open: cin, cout
  ALU_Control alu_control_1 (
    .ALUOp1(control_unit_1_aluop1), .ALUOp0(control_unit_1_aluop0), .Funct(multiplexer_3_out),
    .Operation(alu_control_1_operation));
  Multiplexer #(.width(16), .enable("false")) multiplexer_4 (
    .in0(adder_1_out), .in1(adder_2_out), .out(multiplexer_4_out), .sel(multiplexer_6_out));
  and and_1 (and_1_out, control_unit_1_branch, alu_1_zero);
  and and_2 (and_2_out, control_unit_1_branch, not_1_out);
  Multiplexer #(.width(16), .enable("false")) multiplexer_5 (
    .in0(multiplexer_4_out), .in1(bit_extender_1_out[17:2]), .out(multiplexer_5_out),
    .sel(control_unit_1_jump));
  Multiplexer #(.enable("false")) multiplexer_6 (
    .in0(and_1_out), .in1(and_2_out), .out(multiplexer_6_out), .sel(control_unit_1_bne));

  // Notes on the sheet:
  //   Click to tick
  //   From $t8
  //   From $t9
  //   Write Data to $t9
  //   Write Signal for $t9
  //   funct
  //   shamt
endmodule

module LCD_Controller (
  input  [31:0] From__t8,
  output [6:0] Minus,
  output [6:0] _7_Segment_9,
  output [6:0] _7_Segment_8,
  output [6:0] _7_Segment_7,
  output [6:0] _7_Segment_6,
  output [6:0] _7_Segment_5,
  output [6:0] _7_Segment_4,
  output [6:0] _7_Segment_3,
  output [6:0] _7_Segment_2,
  output [6:0] _7_Segment_1,
  output [6:0] _7_Segment_0
);

  wire [3:0] binarytobcd_1_bcd0, binarytobcd_1_bcd1, binarytobcd_1_bcd2, binarytobcd_1_bcd3,
       binarytobcd_1_bcd4, binarytobcd_1_bcd5, binarytobcd_1_bcd6, binarytobcd_1_bcd7, binarytobcd_1_bcd8,
       binarytobcd_1_bcd9;

  BinaryToBCD binarytobcd_1 (
    .Input(From__t8), .Minus(Minus[0]), .BCD9(binarytobcd_1_bcd9), .BCD8(binarytobcd_1_bcd8),
    .BCD7(binarytobcd_1_bcd7), .BCD6(binarytobcd_1_bcd6), .BCD5(binarytobcd_1_bcd5),
    .BCD4(binarytobcd_1_bcd4), .BCD3(binarytobcd_1_bcd3), .BCD2(binarytobcd_1_bcd2),
    .BCD1(binarytobcd_1_bcd1), .BCD0(binarytobcd_1_bcd0));
  _7_Segment_Controller u_7_segment_controller_1 (.BCD(binarytobcd_1_bcd9), .out_2(_7_Segment_9));
  _7_Segment_Controller u_7_segment_controller_2 (.BCD(binarytobcd_1_bcd8), .out_2(_7_Segment_8));
  _7_Segment_Controller u_7_segment_controller_3 (.BCD(binarytobcd_1_bcd7), .out_2(_7_Segment_7));
  _7_Segment_Controller u_7_segment_controller_4 (.BCD(binarytobcd_1_bcd6), .out_2(_7_Segment_6));
  _7_Segment_Controller u_7_segment_controller_5 (.BCD(binarytobcd_1_bcd5), .out_2(_7_Segment_5));
  _7_Segment_Controller u_7_segment_controller_6 (.BCD(binarytobcd_1_bcd4), .out_2(_7_Segment_4));
  _7_Segment_Controller u_7_segment_controller_7 (.BCD(binarytobcd_1_bcd3), .out_2(_7_Segment_3));
  _7_Segment_Controller u_7_segment_controller_8 (.BCD(binarytobcd_1_bcd2), .out_2(_7_Segment_2));
  _7_Segment_Controller u_7_segment_controller_9 (.BCD(binarytobcd_1_bcd1), .out_2(_7_Segment_1));
  _7_Segment_Controller u_7_segment_controller_10 (.BCD(binarytobcd_1_bcd0), .out_2(_7_Segment_0));

  assign Minus[6:1] = {6{1'b0}};
endmodule

module _7_Segment_Controller (
  input  [3:0] BCD,
  output [6:0] out_2
);

  wire and_1_out, and_2_out, and_3_out, and_4_out, and_5_out, and_6_out, and_7_out, and_8_out, and_9_out,
       and_10_out, and_11_out, and_12_out, and_13_out, and_14_out, and_15_out, and_16_out, not_1_out,
       not_2_out, not_3_out, not_4_out, not_5_out, not_6_out, not_7_out, not_8_out, not_9_out, not_10_out,
       not_11_out, not_12_out, not_13_out, not_14_out, not_15_out, not_16_out, not_17_out, not_18_out,
       not_19_out, not_20_out, not_21_out;

  not not_1 (not_1_out, BCD[2]);
  not not_2 (not_2_out, BCD[0]);
  not not_3 (not_3_out, BCD[1]);
  not not_4 (not_4_out, BCD[1]);
  not not_5 (not_5_out, BCD[0]);
  not not_6 (not_6_out, BCD[1]);
  not not_7 (not_7_out, BCD[0]);
  not not_8 (not_8_out, BCD[2]);
  not not_9 (not_9_out, BCD[0]);
  not not_10 (not_10_out, BCD[1]);
  not not_11 (not_11_out, BCD[0]);
  not not_12 (not_12_out, BCD[2]);
  not not_13 (not_13_out, BCD[0]);
  not not_14 (not_14_out, BCD[0]);
  not not_15 (not_15_out, BCD[2]);
  not not_16 (not_16_out, BCD[0]);
  not not_17 (not_17_out, BCD[2]);
  not not_18 (not_18_out, BCD[0]);
  not not_19 (not_19_out, BCD[1]);
  not not_20 (not_20_out, BCD[1]);
  and and_1 (and_1_out, not_1_out, BCD[1]);
  and and_2 (and_2_out, BCD[1], not_2_out);
  and and_3 (and_3_out, BCD[2], not_3_out);
  and and_4 (and_4_out, not_4_out, not_5_out);
  and and_5 (and_5_out, BCD[2], not_6_out);
  and and_6 (and_6_out, BCD[2], not_7_out);
  and and_7 (and_7_out, not_8_out, not_9_out);
  and and_8 (and_8_out, BCD[2], BCD[0]);
  not not_21 (not_21_out, BCD[2]);
  and and_9 (and_9_out, not_10_out, not_11_out);
  and and_10 (and_10_out, BCD[1], BCD[0]);
  and and_11 (and_11_out, not_12_out, not_13_out);
  and and_12 (and_12_out, BCD[1], not_14_out);
  and and_13 (and_13_out, not_15_out, not_16_out);
  and and_14 (and_14_out, not_17_out, BCD[1]);
  and and_15 (and_15_out, BCD[1], not_18_out);
  and and_16 (and_16_out, BCD[2], not_19_out, BCD[0]);
  or or_1 (out_2[6], not_20_out, BCD[0], BCD[2]);
  or or_2 (out_2[0], and_1_out, and_2_out, and_3_out, BCD[3]);
  or or_3 (out_2[1], and_4_out, and_5_out, and_6_out, BCD[3]);
  or or_4 (out_2[2], and_7_out, BCD[1], and_8_out, BCD[3]);
  or or_5 (out_2[3], not_21_out, and_9_out, and_10_out);
  or or_6 (out_2[4], and_11_out, and_12_out);
  or or_7 (out_2[5], and_13_out, and_14_out, and_15_out, and_16_out);
endmodule

module BinaryToBCD (
  input  [31:0] Input,
  output Minus,
  output [3:0] BCD9,
  output [3:0] BCD8,
  output [3:0] BCD7,
  output [3:0] BCD6,
  output [3:0] BCD5,
  output [3:0] BCD4,
  output [3:0] BCD3,
  output [3:0] BCD2,
  output [3:0] BCD1,
  output [3:0] BCD0
);

  wire [27:0] subtractor_1_out, subtractor_2_out, subtractor_3_out, subtractor_4_out, subtractor_5_out,
       subtractor_6_out, subtractor_7_out, subtractor_8_out, subtractor_9_out;
  wire [31:0] adder_1_out, divider_1_out, divider_2_out, divider_3_out, divider_4_out, divider_5_out,
       divider_6_out, divider_7_out, divider_8_out, multiplexer_1_out, multiplier_1_out, multiplier_2_out,
       multiplier_3_out, multiplier_4_out, multiplier_5_out, multiplier_6_out, multiplier_7_out,
       multiplier_8_out, multiplier_9_out, not_1_out;
  wire [31:4] divider_9_out;

  assign not_1_out = ~Input;  // NOT_Gate not_1, 32 bits wide
  Adder #(.width(32)) adder_1 (.a(not_1_out), .b(32'h1), .out(adder_1_out));  // open: cin, cout
  Multiplexer #(.width(32)) multiplexer_1 (
    .in0(Input), .in1(adder_1_out), .out(multiplexer_1_out), .sel(Input[31]));  // open: en
  Subtractor #(.width(32)) subtractor_1 (
    .a(multiplexer_1_out), .b(multiplier_1_out), .out({subtractor_1_out, BCD0}));  // open: bin, bout
  Multiplier #(.width(32)) multiplier_1 (.a(divider_1_out), .b(32'ha), .out(multiplier_1_out));  // open: cin, cout
  Divider #(.width(32)) divider_1 (.a(multiplexer_1_out), .b(32'ha), .out(divider_1_out));  // open: upper, rem
  Subtractor #(.width(32)) subtractor_2 (
    .a(divider_1_out), .b(multiplier_2_out), .out({subtractor_2_out, BCD1}));  // open: bin, bout
  Multiplier #(.width(32)) multiplier_2 (.a(divider_2_out), .b(32'ha), .out(multiplier_2_out));  // open: cin, cout
  Divider #(.width(32)) divider_2 (.a(divider_1_out), .b(32'ha), .out(divider_2_out));  // open: upper, rem
  Subtractor #(.width(32)) subtractor_3 (
    .a(divider_2_out), .b(multiplier_3_out), .out({subtractor_3_out, BCD2}));  // open: bin, bout
  Multiplier #(.width(32)) multiplier_3 (.a(divider_3_out), .b(32'ha), .out(multiplier_3_out));  // open: cin, cout
  Divider #(.width(32)) divider_3 (.a(divider_2_out), .b(32'ha), .out(divider_3_out));  // open: upper, rem
  Subtractor #(.width(32)) subtractor_4 (
    .a(divider_3_out), .b(multiplier_4_out), .out({subtractor_4_out, BCD3}));  // open: bin, bout
  Multiplier #(.width(32)) multiplier_4 (.a(divider_4_out), .b(32'ha), .out(multiplier_4_out));  // open: cin, cout
  Divider #(.width(32)) divider_4 (.a(divider_3_out), .b(32'ha), .out(divider_4_out));  // open: upper, rem
  Subtractor #(.width(32)) subtractor_5 (
    .a(divider_4_out), .b(multiplier_5_out), .out({subtractor_5_out, BCD4}));  // open: bin, bout
  Multiplier #(.width(32)) multiplier_5 (.a(divider_5_out), .b(32'ha), .out(multiplier_5_out));  // open: cin, cout
  Divider #(.width(32)) divider_5 (.a(divider_4_out), .b(32'ha), .out(divider_5_out));  // open: upper, rem
  Subtractor #(.width(32)) subtractor_6 (
    .a(divider_5_out), .b(multiplier_6_out), .out({subtractor_6_out, BCD5}));  // open: bin, bout
  Multiplier #(.width(32)) multiplier_6 (.a(divider_6_out), .b(32'ha), .out(multiplier_6_out));  // open: cin, cout
  Divider #(.width(32)) divider_6 (.a(divider_5_out), .b(32'ha), .out(divider_6_out));  // open: upper, rem
  Subtractor #(.width(32)) subtractor_7 (
    .a(divider_6_out), .b(multiplier_7_out), .out({subtractor_7_out, BCD6}));  // open: bin, bout
  Multiplier #(.width(32)) multiplier_7 (.a(divider_7_out), .b(32'ha), .out(multiplier_7_out));  // open: cin, cout
  Divider #(.width(32)) divider_7 (.a(divider_6_out), .b(32'ha), .out(divider_7_out));  // open: upper, rem
  Subtractor #(.width(32)) subtractor_8 (
    .a(divider_7_out), .b(multiplier_8_out), .out({subtractor_8_out, BCD7}));  // open: bin, bout
  Multiplier #(.width(32)) multiplier_8 (.a(divider_8_out), .b(32'ha), .out(multiplier_8_out));  // open: cin, cout
  Divider #(.width(32)) divider_8 (.a(divider_7_out), .b(32'ha), .out(divider_8_out));  // open: upper, rem
  Subtractor #(.width(32)) subtractor_9 (
    .a(divider_8_out), .b(multiplier_9_out), .out({subtractor_9_out, BCD8}));  // open: bin, bout
  Multiplier #(.width(32)) multiplier_9 (
    .a({divider_9_out, BCD9}), .b(32'ha), .out(multiplier_9_out));  // open: cin, cout
  Divider #(.width(32)) divider_9 (.a(divider_8_out), .b(32'ha), .out({divider_9_out, BCD9}));  // open: upper, rem

  assign Minus = Input[31];
endmodule

module Keypad_Controller (
  input  C,
  input  in_2,
  input  in_3,
  input  in_4,
  input  in_5,
  input  in_6,
  input  _9,
  input  _8,
  input  _7,
  input  _6,
  input  _5,
  input  _4,
  input  _3,
  input  _2,
  input  _1,
  input  _0,
  input  [31:0] From__t9,
  output Write,
  output [31:0] Output
);

  wire iszero_1_out_2, iszero_2_out_2;
  wire [3:0] or_4_out;
  wire [15:0] and_1_out;

  and and_1 (and_1_out[0], C, iszero_1_out_2);
  and and_2 (and_1_out[1], in_2, iszero_1_out_2);
  and and_3 (and_1_out[2], in_3, iszero_1_out_2);
  and and_4 (and_1_out[3], in_4, iszero_1_out_2);
  and and_5 (and_1_out[4], in_5, iszero_1_out_2);
  and and_6 (and_1_out[5], in_6, iszero_1_out_2);
  and and_7 (and_1_out[6], _9, iszero_1_out_2);
  and and_8 (and_1_out[7], _8, iszero_1_out_2);
  and and_9 (and_1_out[8], _7, iszero_1_out_2);
  and and_10 (and_1_out[9], _6, iszero_1_out_2);
  and and_11 (and_1_out[10], _5, iszero_1_out_2);
  and and_12 (and_1_out[11], _4, iszero_1_out_2);
  and and_13 (and_1_out[12], _3, iszero_1_out_2);
  and and_14 (and_1_out[13], _2, iszero_1_out_2);
  and and_15 (and_1_out[14], _1, iszero_1_out_2);
  and and_16 (and_1_out[15], _0, iszero_1_out_2);
  isZero iszero_1 (.Input(From__t9), .out_2(iszero_1_out_2));
  or or_1 (or_4_out[3], and_1_out[0], and_1_out[1], and_1_out[2], and_1_out[3], and_1_out[4], and_1_out[5], and_1_out[6], and_1_out[7]);
  or or_2 (or_4_out[2], and_1_out[8], and_1_out[9], and_1_out[10], and_1_out[11], and_1_out[0], and_1_out[1], and_1_out[2], and_1_out[3]);
  or or_3 (or_4_out[1], and_1_out[12], and_1_out[13], and_1_out[9], and_1_out[8], and_1_out[5], and_1_out[4], and_1_out[1], and_1_out[0]);
  or or_4 (or_4_out[0], and_1_out[12], and_1_out[14], and_1_out[10], and_1_out[8], and_1_out[6], and_1_out[4], and_1_out[2], and_1_out[0]);
  isZero iszero_2 (.Input({{16{1'b0}}, and_1_out}), .out_2(iszero_2_out_2));
  not not_1 (Write, iszero_2_out_2);
  assign Output = Write ? {28'h8000000, or_4_out} : 32'bz;  // Controlled_Buffer controlled_buffer_1
endmodule

module isZero (
  input  [31:0] Input,
  output out_2
);

  wire or_1_out;

  or or_1 (or_1_out, Input[0], Input[1], Input[2], Input[3], Input[4], Input[5], Input[6], Input[7], Input[8], Input[9], Input[10], Input[11], Input[12], Input[13], Input[14], Input[15], Input[16], Input[17], Input[18], Input[19], Input[20], Input[21], Input[22], Input[23], Input[24], Input[25], Input[26], Input[27], Input[28], Input[29], Input[30], Input[31]);
  not not_1 (out_2, or_1_out);
endmodule

module Instruction_Memory (
  input  [15:0] _16BitInput,
  output [31:0] MachineCode
);

  ROM #(.addrWidth(16), .dataWidth(32)) rom_1 (.addr(_16BitInput), .data(MachineCode));  // open: sel

  // Notes on the sheet:
  //   contents of rom_1 (hex, n*v repeats v):
  //   11c020 20190000 20010001 10350001 810000f 200a0000 20190000 186020 20150000 20110000 200f0000
  //   200e0000 200d0000 200b0000 20090000 1320ffff 198820 118840 118842 2001000f 1031005d 2001000a
  //   10310011 2001000b 1031000f 2001000c 1031000d 2001000d 1031000b 20080000 2001000e 1031003f 11c020
  //   f7020 f78c0 1ee7820 1ee7820 1f17820 f8820 8100000 20010001 10280004 11400003 ab7c2 20010000 10360027
  //   186020 115020 20010001 1028ffd4 c8820 200f0000 20080001 8100000 1605827 216b0001 18b9820 8100057
  //   20130000 1605827 216b0001 18b6020 11800004 11800017 cb7c2 20010001 10360014 22730001 810003d 18b9820
  //   8100057 20130000 ca020 20100000 20010001 102b0001 810004f c9820 8100057 216bffff 1946020 120b0005
  //   22100001 c9820 8100050 114820 200f0000 138820 1120ffa7 95020 20090000 136020 200b0000 12a0ffa2
  //   8100000 20010001 10310001 8100063 20150001 11400001 8100067 23110000 8100000 185820 200f0000
  //   2001000a 102affda 2001000b 102affc9 2001000c 102affd8 2001000d 102affc9 8100000 20110000 200f0000
  //   200e0000 200d0000 200c0000 200b0000 200a0000 20090000 8100000
endmodule

module Shift_Left (
  input  [31:0] Input,
  input  [4:0] ShiftAmt,
  output [31:0] Output
);

  Shifter #(.width(32)) shifter_1 (.in(Input), .\dist (ShiftAmt), .out(Output));
endmodule

module Shift_Right (
  input  [31:0] Input,
  input  [4:0] ShiftAmt,
  output [31:0] Output
);

  Shifter #(.width(32), .shift("lr")) shifter_1 (.in(Input), .\dist (ShiftAmt), .out(Output));
endmodule

// Sign Extend
module Sign_Extend (
  input  Zero,
  input  [15:0] Input,
  output [31:0] out_3
);

  wire [31:0] bit_extender_1_out;

  assign bit_extender_1_out = {{16{1'b0}}, Input};  // Bit_Extender bit_extender_1
  Multiplexer #(.width(32), .enable("false")) multiplexer_1 (
    .in0({{17{Input[15]}}, Input[14:0]}), .in1(bit_extender_1_out), .out(out_3), .sel(Zero));
endmodule

module Register_File (
  input  [4:0] Read_Register_1,
  input  Write,
  input  Clock,
  input  [4:0] Read_Register_2,
  input  [4:0] Write_Register,
  input  [31:0] Write_Data,
  input  [31:0] Write_to__t9_From_Keypad,
  input  Write_signal_from_keypad,
  output [31:0] Read_Data_1,
  output [31:0] Read_Data_2,
  output [31:0] t8_To_LCD,
  output [31:0] T9_to_Keypad
);

  wire and_1_out, and_2_out, and_3_out, and_4_out, and_5_out, and_6_out, and_7_out, and_8_out, and_9_out,
       and_10_out, and_11_out, and_12_out, and_13_out, and_14_out, and_15_out, and_16_out, and_17_out,
       and_18_out, and_19_out, and_20_out, and_21_out, and_22_out, and_23_out, and_24_out, and_25_out,
       and_26_out, and_27_out, and_28_out, and_29_out, and_30_out, and_31_out, and_32_out,
       controlled_buffer_2_out, decoder_1_out0, decoder_1_out1, decoder_1_out2, decoder_1_out3,
       decoder_1_out4, decoder_1_out5, decoder_1_out6, decoder_1_out7, decoder_1_out8, decoder_1_out9,
       decoder_1_out10, decoder_1_out11, decoder_1_out12, decoder_1_out13, decoder_1_out14, decoder_1_out15,
       decoder_1_out16, decoder_1_out17, decoder_1_out18, decoder_1_out19, decoder_1_out20, decoder_1_out21,
       decoder_1_out22, decoder_1_out23, decoder_1_out24, decoder_1_out25, decoder_1_out26, decoder_1_out27,
       decoder_1_out28, decoder_1_out29, decoder_1_out30, decoder_1_out31, xor_1_out, xor_2_out;
  wire [31:0] controlled_buffer_1_out, Register_0_q, Register_1_q, Register_2_q, Register_3_q, Register_4_q,
       Register_5_q, Register_6_q, Register_7_q, Register_8_q, Register_9_q, Register_10_q, Register_11_q,
       Register_12_q, Register_13_q, Register_14_q, Register_15_q, Register_16_q, Register_17_q,
       Register_18_q, Register_19_q, Register_20_q, Register_21_q, Register_22_q, Register_23_q,
       Register_26_q, Register_27_q, Register_28_q, Register_29_q, Register_30_q, Register_31_q;

  Decoder #(.select(5), .enable("false")) decoder_1 (
    .out0(decoder_1_out0), .out1(decoder_1_out1), .out2(decoder_1_out2), .out3(decoder_1_out3),
    .out4(decoder_1_out4), .out5(decoder_1_out5), .out6(decoder_1_out6), .out7(decoder_1_out7),
    .out8(decoder_1_out8), .out9(decoder_1_out9), .out10(decoder_1_out10), .out11(decoder_1_out11),
    .out12(decoder_1_out12), .out13(decoder_1_out13), .out14(decoder_1_out14), .out15(decoder_1_out15),
    .out16(decoder_1_out16), .out17(decoder_1_out17), .out18(decoder_1_out18), .out19(decoder_1_out19),
    .out20(decoder_1_out20), .out21(decoder_1_out21), .out22(decoder_1_out22), .out23(decoder_1_out23),
    .out24(decoder_1_out24), .out25(decoder_1_out25), .out26(decoder_1_out26), .out27(decoder_1_out27),
    .out28(decoder_1_out28), .out29(decoder_1_out29), .out30(decoder_1_out30), .out31(decoder_1_out31),
    .sel(Write_Register));
  and and_1 (and_1_out, Write, decoder_1_out13);
  and and_2 (and_2_out, Write, decoder_1_out15);
  and and_3 (and_3_out, Write, decoder_1_out16);
  and and_4 (and_4_out, Write, decoder_1_out17);
  and and_5 (and_5_out, Write, decoder_1_out18);
  and and_6 (and_6_out, Write, decoder_1_out19);
  and and_7 (and_7_out, Write, decoder_1_out20);
  and and_8 (and_8_out, Write, decoder_1_out21);
  and and_9 (and_9_out, Write, decoder_1_out22);
  and and_10 (and_10_out, Write, decoder_1_out23);
  and and_11 (and_11_out, Write, decoder_1_out24);
  and and_12 (and_12_out, Write, decoder_1_out25);
  and and_13 (and_13_out, Write, decoder_1_out26);
  and and_14 (and_14_out, Write, decoder_1_out27);
  and and_15 (and_15_out, Write, decoder_1_out28);
  and and_16 (and_16_out, Write, decoder_1_out29);
  and and_17 (and_17_out, Write, decoder_1_out30);
  and and_18 (and_18_out, Write, decoder_1_out31);
  and and_19 (and_19_out, Write, decoder_1_out0);
  and and_20 (and_20_out, Write, decoder_1_out1);
  and and_21 (and_21_out, Write, decoder_1_out2);
  and and_22 (and_22_out, Write, decoder_1_out3);
  and and_23 (and_23_out, Write, decoder_1_out4);
  and and_24 (and_24_out, Write, decoder_1_out5);
  and and_25 (and_25_out, Write, decoder_1_out6);
  and and_26 (and_26_out, Write, decoder_1_out7);
  and and_27 (and_27_out, Write, decoder_1_out8);
  and and_28 (and_28_out, Write, decoder_1_out9);
  and and_29 (and_29_out, Write, decoder_1_out10);
  and and_30 (and_30_out, Write, decoder_1_out11);
  and and_31 (and_31_out, Write, decoder_1_out12);
  and and_32 (and_32_out, Write, decoder_1_out14);
  assign controlled_buffer_1_out = Write_signal_from_keypad ? Write_to__t9_From_Keypad : 32'bz;  // Controlled_Buffer controlled_buffer_1
  assign controlled_buffer_2_out = Write_signal_from_keypad ? Write_signal_from_keypad : 1'bz;  // Controlled_Buffer controlled_buffer_2
  assign controlled_buffer_1_out = and_12_out ? Write_Data : 32'bz;  // Controlled_Buffer controlled_buffer_3
  assign controlled_buffer_2_out = and_12_out ? and_12_out : 1'bz;  // Controlled_Buffer controlled_buffer_4
  Register #(.width(32)) Register_0 (.D(Write_Data), .en(and_19_out), .Q(Register_0_q), .clk(Clock));  // open: clr
  Register #(.width(32)) Register_1 (.D(Write_Data), .en(and_20_out), .Q(Register_1_q), .clk(Clock));  // open: clr
  Register #(.width(32)) Register_2 (.D(Write_Data), .en(and_21_out), .Q(Register_2_q), .clk(Clock));  // open: clr
  Register #(.width(32)) Register_3 (.D(Write_Data), .en(and_22_out), .Q(Register_3_q), .clk(Clock));  // open: clr
  Register #(.width(32)) Register_4 (.D(Write_Data), .en(and_23_out), .Q(Register_4_q), .clk(Clock));  // open: clr
  Register #(.width(32)) Register_5 (.D(Write_Data), .en(and_24_out), .Q(Register_5_q), .clk(Clock));  // open: clr
  Register #(.width(32)) Register_16 (.D(Write_Data), .en(and_3_out), .Q(Register_16_q), .clk(Clock));  // open: clr
  Register #(.width(32)) Register_17 (.D(Write_Data), .en(and_4_out), .Q(Register_17_q), .clk(Clock));  // open: clr
  Register #(.width(32)) Register_18 (.D(Write_Data), .en(and_5_out), .Q(Register_18_q), .clk(Clock));  // open: clr
  Register #(.width(32)) Register_19 (.D(Write_Data), .en(and_6_out), .Q(Register_19_q), .clk(Clock));  // open: clr
  Register #(.width(32)) Register_20 (.D(Write_Data), .en(and_7_out), .Q(Register_20_q), .clk(Clock));  // open: clr
  Register #(.width(32)) Register_21 (.D(Write_Data), .en(and_8_out), .Q(Register_21_q), .clk(Clock));  // open: clr
  Register #(.width(32)) Register_22 (.D(Write_Data), .en(and_9_out), .Q(Register_22_q), .clk(Clock));  // open: clr
  Register #(.width(32)) Register_23 (.D(Write_Data), .en(and_10_out), .Q(Register_23_q), .clk(Clock));  // open: clr
  Register #(.width(32)) Register_24 (.D(Write_Data), .en(and_11_out), .Q(t8_To_LCD), .clk(Clock));  // open: clr
  xor xor_1 (xor_1_out, Clock, Write_signal_from_keypad);
  Register #(.width(32)) Register_26 (.D(Write_Data), .en(and_13_out), .Q(Register_26_q), .clk(Clock));  // open: clr
  Register #(.width(32)) Register_6 (.D(Write_Data), .en(and_25_out), .Q(Register_6_q), .clk(Clock));  // open: clr
  Register #(.width(32)) Register_7 (.D(Write_Data), .en(and_26_out), .Q(Register_7_q), .clk(Clock));  // open: clr
  Register #(.width(32)) Register_8 (.D(Write_Data), .en(and_27_out), .Q(Register_8_q), .clk(Clock));  // open: clr
  Register #(.width(32)) Register_9 (.D(Write_Data), .en(and_28_out), .Q(Register_9_q), .clk(Clock));  // open: clr
  Register #(.width(32)) Register_10 (.D(Write_Data), .en(and_29_out), .Q(Register_10_q), .clk(Clock));  // open: clr
  Register #(.width(32)) Register_11 (.D(Write_Data), .en(and_30_out), .Q(Register_11_q), .clk(Clock));  // open: clr
  Register #(.width(32)) Register_12 (.D(Write_Data), .en(and_31_out), .Q(Register_12_q), .clk(Clock));  // open: clr
  Register #(.width(32)) Register_13 (.D(Write_Data), .en(and_1_out), .Q(Register_13_q), .clk(Clock));  // open: clr
  Register #(.width(32)) Register_14 (.D(Write_Data), .en(and_32_out), .Q(Register_14_q), .clk(Clock));  // open: clr
  Register #(.width(32)) Register_15 (.D(Write_Data), .en(and_2_out), .Q(Register_15_q), .clk(Clock));  // open: clr
  xor xor_2 (xor_2_out, Clock, xor_1_out);
  Register #(.width(32)) Register_27 (.D(Write_Data), .en(and_14_out), .Q(Register_27_q), .clk(Clock));  // open: clr
  Register #(.width(32)) Register_28 (.D(Write_Data), .en(and_15_out), .Q(Register_28_q), .clk(Clock));  // open: clr
  Register #(.width(32)) Register_29 (.D(Write_Data), .en(and_16_out), .Q(Register_29_q), .clk(Clock));  // open: clr
  Register #(.width(32)) Register_30 (.D(Write_Data), .en(and_17_out), .Q(Register_30_q), .clk(Clock));  // open: clr
  Register #(.width(32)) Register_31 (.D(Write_Data), .en(and_18_out), .Q(Register_31_q), .clk(Clock));  // open: clr
  Register #(.width(32)) Register_25 (
    .D(controlled_buffer_1_out), .en(controlled_buffer_2_out), .Q(T9_to_Keypad), .clk(xor_2_out));  // open: clr
  Multiplexer #(.select(5), .width(32), .enable("false")) multiplexer_1 (
    .in0(Register_0_q), .in1(Register_1_q), .in2(Register_2_q), .in3(Register_3_q), .in4(Register_4_q),
    .in5(Register_5_q), .in6(Register_6_q), .in7(Register_7_q), .in8(Register_8_q), .in9(Register_9_q),
    .in10(Register_10_q), .in11(Register_11_q), .in12(Register_12_q), .in13(Register_13_q),
    .in14(Register_14_q), .in15(Register_15_q), .in16(Register_16_q), .in17(Register_17_q),
    .in18(Register_18_q), .in19(Register_19_q), .in20(Register_20_q), .in21(Register_21_q),
    .in22(Register_22_q), .in23(Register_23_q), .in24(t8_To_LCD), .in25(T9_to_Keypad), .in26(Register_26_q),
    .in27(Register_27_q), .in28(Register_28_q), .in29(Register_29_q), .in30(Register_30_q),
    .in31(Register_31_q), .out(Read_Data_2), .sel(Read_Register_2));
  Multiplexer #(.select(5), .width(32), .enable("false")) multiplexer_2 (
    .in0(Register_0_q), .in1(Register_1_q), .in2(Register_2_q), .in3(Register_3_q), .in4(Register_4_q),
    .in5(Register_5_q), .in6(Register_6_q), .in7(Register_7_q), .in8(Register_8_q), .in9(Register_9_q),
    .in10(Register_10_q), .in11(Register_11_q), .in12(Register_12_q), .in13(Register_13_q),
    .in14(Register_14_q), .in15(Register_15_q), .in16(Register_16_q), .in17(Register_17_q),
    .in18(Register_18_q), .in19(Register_19_q), .in20(Register_20_q), .in21(Register_21_q),
    .in22(Register_22_q), .in23(Register_23_q), .in24(t8_To_LCD), .in25(T9_to_Keypad), .in26(Register_26_q),
    .in27(Register_27_q), .in28(Register_28_q), .in29(Register_29_q), .in30(Register_30_q),
    .in31(Register_31_q), .out(Read_Data_1), .sel(Read_Register_1));

  // Notes on the sheet:
  //   OUTPUTS
endmodule

// Control
module Control_Unit (
  input  [5:0] OpCode,
  output RegDst,
  output Jump,
  output Branch,
  output MemRead,
  output MemtoReg,
  output ALUOp0,
  output MemWrite,
  output ALUSrc,
  output RegWrite,
  output ALUOp1,
  output ZeroExtendImm,
  output BNE
);

  wire and_4_out, and_6_out, and_8_out, and_9_out, not_1_out, not_2_out, not_3_out, not_4_out, not_5_out,
       not_6_out, not_7_out, not_8_out, not_9_out, not_10_out, not_11_out, not_12_out, not_13_out,
       not_14_out, not_15_out, not_16_out, not_17_out, not_18_out, not_19_out, not_20_out, not_21_out,
       not_22_out, not_23_out, not_24_out, not_25_out, not_26_out, not_27_out, not_28_out, not_29_out,
       not_30_out, not_31_out, not_32_out, not_33_out, not_34_out, not_35_out, not_36_out, not_37_out,
       not_38_out, not_39_out, not_40_out, not_41_out, or_1_out, or_2_out, or_3_out, or_4_out, or_5_out,
       or_6_out, or_7_out, or_8_out, or_9_out, or_10_out;

  not not_1 (not_1_out, OpCode[5]);
  not not_2 (not_2_out, OpCode[3]);
  not not_3 (not_3_out, OpCode[2]);
  not not_4 (not_4_out, OpCode[4]);
  not not_5 (not_5_out, OpCode[1]);
  not not_6 (not_6_out, OpCode[0]);
  and and_1 (RegDst, not_1_out, not_4_out, not_2_out, not_3_out, not_5_out, not_6_out);
  not not_7 (not_7_out, OpCode[4]);
  not not_8 (not_8_out, OpCode[3]);
  not not_9 (not_9_out, OpCode[2]);
  and and_2 (MemRead, OpCode[5], not_7_out, not_8_out, not_9_out, OpCode[1], OpCode[0]);
  not not_10 (not_10_out, OpCode[2]);
  not not_11 (not_11_out, OpCode[4]);
  and and_3 (MemWrite, OpCode[5], not_11_out, OpCode[3], not_10_out, OpCode[1], OpCode[0]);
  not not_12 (not_12_out, OpCode[3]);
  not not_13 (not_13_out, OpCode[5]);
  not not_14 (not_14_out, OpCode[1]);
  not not_15 (not_15_out, OpCode[4]);
  and and_4 (and_4_out, not_13_out, not_15_out, not_12_out, OpCode[2], not_14_out, not_16_out);
  not not_16 (not_16_out, OpCode[0]);
  not not_17 (not_17_out, OpCode[3]);
  not not_18 (not_18_out, OpCode[4]);
  not not_19 (not_19_out, OpCode[5]);
  and and_5 (Jump, not_19_out, not_18_out, not_17_out, not_22_out, OpCode[1], not_23_out);
  or or_1 (or_1_out, MemRead, MemWrite);
  not not_20 (not_20_out, OpCode[4]);
  not not_21 (not_21_out, OpCode[5]);
  not not_22 (not_22_out, OpCode[2]);
  not not_23 (not_23_out, OpCode[0]);
  or or_2 (or_2_out, RegDst, MemRead);
  not not_24 (not_24_out, OpCode[0]);
  not not_25 (not_25_out, OpCode[1]);
  not not_26 (not_26_out, OpCode[2]);
  not not_27 (not_27_out, OpCode[5]);
  and and_6 (and_6_out, not_21_out, not_20_out, OpCode[3], not_26_out, not_25_out, not_24_out);
  or or_3 (or_3_out, and_6_out, RegDst);
  not not_28 (not_28_out, OpCode[0]);
  not not_29 (not_29_out, OpCode[4]);
  not not_30 (not_30_out, OpCode[1]);
  and and_7 (ZeroExtendImm, not_27_out, not_29_out, OpCode[3], OpCode[2], not_30_out, not_28_out);
  or or_4 (or_4_out, and_6_out, or_2_out);
  not not_31 (not_31_out, OpCode[5]);
  not not_32 (not_32_out, OpCode[4]);
  and and_8 (and_8_out, not_31_out, not_32_out, OpCode[3], OpCode[2], not_33_out, OpCode[0]);
  or or_5 (or_5_out, and_6_out, or_1_out);
  not not_33 (not_33_out, OpCode[1]);
  or or_6 (or_6_out, or_5_out, ZeroExtendImm);
  or or_7 (or_7_out, and_8_out, and_4_out);
  not not_34 (not_34_out, OpCode[4]);
  not not_35 (not_35_out, OpCode[2]);
  not not_36 (not_36_out, OpCode[5]);
  and and_9 (and_9_out, not_36_out, not_34_out, OpCode[3], not_35_out, OpCode[1], not_37_out);
  or or_8 (or_8_out, ZeroExtendImm, or_4_out);
  not not_37 (not_37_out, OpCode[0]);
  not not_38 (not_38_out, OpCode[5]);
  not not_39 (not_39_out, OpCode[4]);
  not not_40 (not_40_out, OpCode[3]);
  not not_41 (not_41_out, OpCode[1]);
  and and_10 (BNE, not_38_out, not_39_out, not_40_out, OpCode[2], not_41_out, OpCode[0]);
  or or_9 (or_9_out, and_8_out, or_6_out);
  or or_10 (or_10_out, and_8_out, or_8_out);
  or or_11 (ALUOp0, BNE, or_7_out);
  or or_12 (ALUOp1, and_9_out, or_3_out);
  or or_13 (ALUSrc, and_9_out, or_9_out);
  or or_14 (RegWrite, and_9_out, or_10_out);
  or or_15 (Branch, and_4_out, BNE);

  assign MemtoReg = MemRead;

  // Notes on the sheet:
  //   R-format
  //   lw
  //   sw
  //   beq
  //   jump
  //   addi
  //   andi
  //   ori
  //   slt
  //   bne
endmodule

module ALU (
  input  [3:0] Operation,
  input  Binvert,
  input  CarryIn,
  input  [31:0] A,
  input  [31:0] B,
  input  [4:0] Shamt,
  input  [1:0] ShiftOperation,
  output Zero,
  output Set,
  output [31:0] Result,
  output CarryOut
);

  wire [31:0] adder_1_out, and_1_out, bit_extender_1_out, multiplexer_1_out, multiplexer_2_out,
       multiplexer_4_out, nor_1_out, not_1_out, or_1_out, shift_left_1_output, shift_right_1_output,
       subtractor_1_out;

  assign not_1_out = ~B;  // NOT_Gate not_1, 32 bits wide
  Multiplexer #(.width(32), .enable("false")) multiplexer_1 (
    .in0(B), .in1(not_1_out), .out(multiplexer_1_out), .sel(Binvert));
  Shift_Left shift_left_1 (.Input(B), .ShiftAmt(Shamt), .Output(shift_left_1_output));
  Shift_Right shift_right_1 (.Input(B), .ShiftAmt(Shamt), .Output(shift_right_1_output));
  assign and_1_out = A & multiplexer_1_out;  // AND_Gate and_1, 32 bits wide
  assign or_1_out = A | multiplexer_1_out;  // OR_Gate or_1, 32 bits wide
  Adder #(.width(32)) adder_1 (.a(A), .b(multiplexer_1_out), .out(adder_1_out), .cin(CarryIn), .cout(CarryOut));
  Subtractor #(.width(32)) subtractor_1 (.a(A), .b(multiplexer_1_out), .out(subtractor_1_out));  // open: bin, bout
  Comparator #(.width(32)) comparator_1 (.a(A), .b(multiplexer_1_out), .lt(Set));  // open: gt, eq
  assign nor_1_out = ~(A | multiplexer_1_out);  // NOR_Gate nor_1, 32 bits wide
  Multiplexer #(.select(4), .width(32), .enable("false")) multiplexer_2 (
    .in0(and_1_out), .in1(or_1_out), .in2(adder_1_out), .in6(subtractor_1_out), .in12(nor_1_out),
    .out(multiplexer_2_out), .sel(Operation));  // open: in3, in4, in5, in7, in8, in9, in10, in11, in13, in14, in15
  Multiplexer #(.select(2), .width(32), .enable("false")) multiplexer_3 (
    .in0(multiplexer_2_out), .in2(shift_left_1_output), .in3(shift_right_1_output), .out(Result),
    .sel(ShiftOperation));  // open: in1
  assign bit_extender_1_out = {{31{1'b0}}, Set};  // Bit_Extender bit_extender_1
  Multiplexer #(.select(4), .width(32), .enable("false")) multiplexer_4 (
    .in0(multiplexer_2_out), .in1(multiplexer_2_out), .in2(multiplexer_2_out), .in3(multiplexer_2_out),
    .in4(multiplexer_2_out), .in5(multiplexer_2_out), .in6(multiplexer_2_out), .in7(bit_extender_1_out),
    .in8(multiplexer_2_out), .in9(multiplexer_2_out), .in10(multiplexer_2_out), .in11(multiplexer_2_out),
    .in12(multiplexer_2_out), .in13(multiplexer_2_out), .in14(multiplexer_2_out), .in15(multiplexer_2_out),
    .out(multiplexer_4_out), .sel(Operation));
  isZero iszero_1 (.Input(multiplexer_4_out), .out_2(Zero));
endmodule

module Shift_Left_26_bIt (
  input  [25:0] Input,
  input  [4:0] ShiftAmt,
  output [25:0] Output
);

  Shifter #(.width(26)) shifter_1 (.in(Input), .\dist (ShiftAmt), .out(Output));
endmodule

module Shift_Operations (
  input  [5:0] Funct,
  output ALUOp2,
  output ALUOp3
);

  wire and_1_out, not_1_out, not_2_out, not_3_out, not_4_out, not_5_out, not_6_out, not_7_out, not_8_out,
       not_9_out, not_10_out, not_11_out;

  not not_1 (not_1_out, Funct[1]);
  not not_2 (not_2_out, Funct[0]);
  and and_1 (and_1_out, not_2_out, not_1_out, not_6_out, not_3_out, not_7_out, not_4_out);
  not not_3 (not_3_out, Funct[3]);
  not not_4 (not_4_out, Funct[5]);
  not not_5 (not_5_out, Funct[0]);
  not not_6 (not_6_out, Funct[2]);
  not not_7 (not_7_out, Funct[4]);
  and and_2 (ALUOp2, not_5_out, Funct[1], not_10_out, not_9_out, not_8_out, not_11_out);
  not not_8 (not_8_out, Funct[4]);
  not not_9 (not_9_out, Funct[3]);
  not not_10 (not_10_out, Funct[2]);
  not not_11 (not_11_out, Funct[5]);
  Multiplexer #(.enable("false")) multiplexer_1 (.in0(and_1_out), .in1(ALUOp2), .out(ALUOp3), .sel(ALUOp2));
endmodule

module ALU_Control (
  input  ALUOp1,
  input  ALUOp0,
  input  [5:0] Funct,
  output [3:0] Operation
);

  wire and_1_out, and_3_out, not_1_out, not_2_out, not_3_out, not_4_out, or_1_out;
  wire [2:0] and_2_out;

  or or_1 (or_1_out, Funct[3], Funct[0]);
  not not_1 (not_1_out, Funct[4]);
  not not_2 (not_2_out, Funct[3]);
  and and_1 (and_1_out, ALUOp1, Funct[1]);
  not not_3 (not_3_out, ALUOp1);
  not not_4 (not_4_out, Funct[2]);
  and and_2 (and_2_out[0], ALUOp1, or_1_out);
  and and_3 (and_3_out, Funct[5], not_1_out, not_2_out, Funct[2], Funct[1], Funct[0]);
  or or_2 (and_2_out[2], ALUOp0, and_1_out);
  or or_3 (and_2_out[1], not_3_out, not_4_out);
  Multiplexer #(.width(4), .disabled(0), .enable("false")) multiplexer_1 (
    .in0({1'b0, and_2_out}), .in1(4'b1100), .out(Operation), .sel(and_3_out));
endmodule
